# Fritzing sketch servo-Rpi3 (saved by Fritzing 0.8.7b)
breadboards: 1

parts:
  Raspberry_Pi_1 = Raspberry Pi 3 [part_number=RPI-3-V1.2]
  SERVO1 = Tower Pro SG90 servo [part_number=101246]
  SERVO2 = Tower Pro SG90 servo [part_number=101246]
  SERVO3 = Tower Pro SG90 servo [part_number=101246]
  SERVO4 = Tower Pro SG90 servo [part_number=101246]

nets:
  N1: Raspberry_Pi_1.GIPO6, SERVO4.Signal
  N2: Raspberry_Pi_1.GIPO13, SERVO3.Signal
  N3: Raspberry_Pi_1.GIPO19, SERVO1.Signal
  N4: Raspberry_Pi_1.GIPO26, SERVO2.Signal
  GND: Raspberry_Pi_1.GND, SERVO1.GND, SERVO2.GND, SERVO3.GND, SERVO4.GND
  +5V: Raspberry_Pi_1.5V, SERVO1.+5V, SERVO2.+5V, SERVO3.+5V, SERVO4.+5V

custom parts:
  Tower Pro SG90 servo: Original file by John De Cristofaro http://www.adafruit.com/products/1449 Adafruit Feedback Servo (Small) Edited by: e-radionica.com 28/9/2015
